// Logisim project COMPUTER_One.circ as structural Verilog: 5 circuits, main circuit main
module main (
);

  wire AccumulatorEquals, AccuOut, ACUEQU, ADD, Carry, CarryIn, Clk, CNT, CNTOVER, CNTOVERFLOW, DataEquals,
       DATEQU, FLAG, IsCarry, IsZero, jmp_1_pcload, JMPACUEQU, JMPCARRY, JMPCNTOVER, JMPDATA, JMPDATEQU,
       JMPZERO, JUMP, LOAD, register_2_q, ResetAccu, RomToData, SAVE, SetA, SetCount, SetEqualREG, Sub,
       WriteOut, Zero;
  wire [7:0] binairy_to_bcd_converter_1_p1, counter_1_q, Data, jmp_1_pcin, ROMData;
  wire [11:8] rom_1_data;

  // BCD_to_7_Segment_decoder bcd_to_7_segment_decoder_1: pin names not known
  _7_Segment_Display u_7_segment_display_1 ();  // open: g, f, a, b, e, d, c, dp
  // Binairy_to_BCD_converter #(.binvalue(8)) binairy_to_bcd_converter_1: pin names not known; wires that end beside it: binairy_to_bcd_converter_1_p1
  Register register_1 (.D(Data), .en(WriteOut), .clk(Clk), .Q(binairy_to_bcd_converter_1_p1));  // open: clr
  _7_Segment_Display u_7_segment_display_2 ();  // open: g, f, a, b, e, d, c, dp
  _7_Segment_Display u_7_segment_display_3 ();  // open: g, f, a, b, e, d, c, dp
  // BCD_to_7_Segment_decoder bcd_to_7_segment_decoder_2: pin names not known
  // BCD_to_7_Segment_decoder bcd_to_7_segment_decoder_3: pin names not known
  Hex_Digit_Display hex_digit_display_1 (.value(Data[3:0]));  // open: dp
  Hex_Digit_Display hex_digit_display_2 (.value(Data[7:4]));  // open: dp
  assign Data = RomToData ? ROMData : 8'bz;  // Controlled_Buffer controlled_buffer_1
  Pull_Resistor pull_resistor_1 (.node(Data));
  JMP jmp_1 (
    .JMP(JUMP), .JMPZERO(JMPZERO), .ZERO(Zero), .JMPCARRY(JMPCARRY), .CARRY(Carry), .JMPDATA(JMPDATA),
    .JMPACUEQU(JMPACUEQU), .ACUEQU(ACUEQU), .JMPDATEQU(JMPDATEQU), .DATEQU(DATEQU), .JMPCNTOVER(JMPCNTOVER),
    .CNTOVER(CNTOVER), .ROM(ROMData), .DATA(Data), .PCIn(jmp_1_pcin), .PCLoad(jmp_1_pcload));
  Counter #(.ongoal("stay")) counter_1 (
    .clr(1'b0), .load(jmp_1_pcload), .up(1'b1), .count(1'b1), .clk(Clk), .D(jmp_1_pcin), .Q(counter_1_q));  // open: carry
  ROM #(.dataWidth(12)) rom_1 (.addr(counter_1_q), .data({rom_1_data, ROMData}));
  Count count_1 (
    .Count(CNT), .ROM(ROMData), .DATA(Data), .SetCount(SetCount), .Clock(Clk), .CNTOUT(Data),
    .CNTOverflow(CNTOVERFLOW));
  Clock clock_1 (.out(Clk));
  FLG flg_1 (
    .FLG(FLAG), .ROM(ROMData), .IsCarry(IsCarry), .IsZero(IsZero), .AccumulatorEquals(AccumulatorEquals),
    .DataEquals(DataEquals), .Clock(Clk), .CNTOverflow(CNTOVERFLOW), .WriteOut(WriteOut), .AccuOut(AccuOut),
    .RomToData(RomToData), .Carry(Carry), .Zero(Zero), .Sub(Sub), .CarryIn(CarryIn),
    .ResetAccumulator(ResetAccu), .AcuEqu(ACUEQU), .DatEqu(DATEQU), .CNTOverFlag(CNTOVER));
  ALU alu_1 (
    .Sub(Sub), .CarryIn(CarryIn), .Ain(Data), .SetA(SetA), .AccumulatorOut(AccuOut), .Add(ADD),
    .ResetAcum(ResetAccu), .SetEqualREG(SetEqualREG), .Clock(Clk), .Accumulator(Data),
    .AccumulatorIsZero(IsZero), .CarryOut(IsCarry), .DataEquals(DataEquals),
    .AccumulatorEquals(AccumulatorEquals));
  Decoder #(.select(4), .enable("false")) decoder_1 (
    .out1(FLAG), .out2(JUMP), .out3(JMPDATA), .out4(JMPZERO), .out5(JMPCARRY), .out6(JMPACUEQU),
    .out7(JMPDATEQU), .out8(ADD), .out9(SetA), .out10(SetEqualREG), .out11(SetCount), .out12(SAVE),
    .out13(CNT), .out14(LOAD), .out15(JMPCNTOVER), .sel(rom_1_data));  // open: out0
  Register #(.width(1)) register_2 (.D(ROMData[4]), .en(LOAD), .clk(Clk), .Q(register_2_q));  // open: clr
  RAM ram_1 (.addr(ROMData), .we(SAVE), .oe(register_2_q), .clk(Clk), .data(Data));

  // Notes on the sheet:
  //   contents of rom_1 (hex, n*v repeats v):
  //   140 902 130 800 800 150 120 100 208
endmodule

module JMP (
  input  JMP,
  input  JMPZERO,
  input  ZERO,
  input  JMPCARRY,
  input  CARRY,
  input  JMPDATA,
  input  JMPACUEQU,
  input  ACUEQU,
  input  JMPDATEQU,
  input  DATEQU,
  input  JMPCNTOVER,
  input  CNTOVER,
  input  [7:0] ROM,
  input  [7:0] DATA,
  output [7:0] PCIn,
  output PCLoad
);

  wire and_1_out, and_2_out, and_3_out, and_4_out, and_5_out;

  and and_1 (and_1_out, JMPZERO, ZERO);
  and and_2 (and_2_out, JMPCARRY, CARRY);
  and and_3 (and_3_out, JMPACUEQU, ACUEQU);
  and and_4 (and_4_out, JMPDATEQU, DATEQU);
  and and_5 (and_5_out, JMPCNTOVER, CNTOVER);
  Multiplexer #(.width(8), .enable("false")) multiplexer_1 (.in0(ROM), .in1(DATA), .out(PCIn), .sel(JMPDATA));
  or or_1 (PCLoad, JMP, and_1_out, and_2_out, JMPDATA, and_3_out, and_4_out, and_5_out);
endmodule

module ALU (
  input  Sub,
  input  CarryIn,
  input  [7:0] Ain,
  input  SetA,
  input  AccumulatorOut,
  input  Add,
  input  ResetAcum,
  input  SetEqualREG,
  input  Clock,
  output [7:0] Accumulator,
  output AccumulatorIsZero,
  output CarryOut,
  output DataEquals,
  output AccumulatorEquals
);

  wire or_1_out;
  wire [7:0] adder_1_out, multiplexer_1_out, negator_1_out, register_1_q, register_2_q, register_3_q;

  Register register_1 (.D(Ain), .en(SetEqualREG), .clk(Clock), .Q(register_1_q));  // open: clr
  Register register_2 (.D(Ain), .en(SetA), .clk(Clock), .Q(register_2_q));  // open: clr
  Negator negator_1 (.in(register_2_q), .out(negator_1_out));
  Comparator comparator_1 (.a(Ain), .b(register_1_q), .eq(DataEquals));  // open: gt, lt
  Multiplexer #(.width(8), .enable("false")) multiplexer_1 (
    .in0(register_2_q), .in1(negator_1_out), .out(multiplexer_1_out), .sel(Sub));
  Adder adder_1 (.a(multiplexer_1_out), .b(register_3_q), .out(adder_1_out), .cin(CarryIn), .cout(CarryOut));
  Register register_3 (.D(adder_1_out), .en(Add), .clk(Clock), .Q(register_3_q), .clr(ResetAcum));
  assign Accumulator = AccumulatorOut ? register_3_q : 8'bz;  // Controlled_Buffer controlled_buffer_1
  Comparator comparator_2 (.a(register_3_q), .b(register_1_q), .eq(AccumulatorEquals));  // open: gt, lt
  or or_1 (or_1_out, register_3_q[0], register_3_q[1], register_3_q[2], register_3_q[3], register_3_q[4], register_3_q[5], register_3_q[6], register_3_q[7]);
  not not_1 (AccumulatorIsZero, or_1_out);
endmodule

module FLG (
  input  FLG,
  input  [7:0] ROM,
  input  IsCarry,
  input  IsZero,
  input  AccumulatorEquals,
  input  DataEquals,
  input  Clock,
  input  CNTOverflow,
  output WriteOut,
  output AccuOut,
  output RomToData,
  output Carry,
  output Zero,
  output Sub,
  output CarryIn,
  output ResetAccumulator,
  output AcuEqu,
  output DatEqu,
  output CNTOverFlag
);

  wire decoder_1_out0, decoder_1_out1, decoder_1_out2, decoder_1_out3, decoder_1_out4, decoder_1_out5,
       decoder_1_out6, decoder_1_out7, decoder_1_out8, decoder_1_out9, decoder_1_out10, decoder_1_out11,
       decoder_1_out13, decoder_1_out14, decoder_1_out15;

  Decoder #(.select(4), .enable("false")) decoder_1 (
    .out0(decoder_1_out0), .out1(decoder_1_out1), .out2(decoder_1_out2), .out3(decoder_1_out3),
    .out4(decoder_1_out4), .out5(decoder_1_out5), .out6(decoder_1_out6), .out7(decoder_1_out7),
    .out8(decoder_1_out8), .out9(decoder_1_out9), .out10(decoder_1_out10), .out11(decoder_1_out11),
    .out12(ResetAccumulator), .out13(decoder_1_out13), .out14(decoder_1_out14), .out15(decoder_1_out15),
    .sel(ROM[7:4]));
  S_R_Flip_Flop WriteOutf (
    .S(decoder_1_out0), .R(decoder_1_out1), .clk(Clock), .Q(WriteOut), .reset(decoder_1_out15));  // open: Qn, preset
  S_R_Flip_Flop AccuOutf (
    .S(decoder_1_out2), .R(decoder_1_out3), .clk(Clock), .Q(AccuOut), .reset(decoder_1_out15));  // open: Qn, preset
  S_R_Flip_Flop RomToDataf (
    .S(decoder_1_out4), .R(decoder_1_out5), .clk(Clock), .Q(RomToData), .reset(decoder_1_out15));  // open: Qn, preset
  S_R_Flip_Flop Carryf (
    .S(IsCarry), .R(decoder_1_out6), .clk(Clock), .Q(Carry), .reset(decoder_1_out15));  // open: Qn, preset
  S_R_Flip_Flop Zerof (
    .S(IsZero), .R(decoder_1_out7), .clk(Clock), .Q(Zero), .reset(decoder_1_out15));  // open: Qn, preset
  S_R_Flip_Flop Subf (
    .S(decoder_1_out8), .R(decoder_1_out9), .clk(Clock), .Q(Sub), .reset(decoder_1_out15));  // open: Qn, preset
  S_R_Flip_Flop CarryInf (
    .S(decoder_1_out10), .R(decoder_1_out11), .clk(Clock), .Q(CarryIn), .reset(decoder_1_out15));  // open: Qn, preset
  S_R_Flip_Flop AccumEqualsf (
    .S(AccumulatorEquals), .R(decoder_1_out13), .clk(Clock), .Q(AcuEqu), .reset(decoder_1_out15));  // open: Qn, preset
  S_R_Flip_Flop s_r_ff_1 (
    .S(CNTOverflow), .R(decoder_1_out14), .clk(Clock), .Q(CNTOverFlag));  // open: reset, Qn, preset

  assign DatEqu = DataEquals;
endmodule

module Count (
  input  Count,
  input  [7:0] ROM,
  input  [7:0] DATA,
  input  SetCount,
  input  Clock,
  output [7:0] CNTOUT,
  output CNTOverflow
);

  wire decoder_1_out0, decoder_1_out1, decoder_1_out2, decoder_1_out3, decoder_1_out4, or_1_out, or_2_out,
       s_r_ff_1_q;
  wire [7:0] counter_1_q;

  Decoder #(.select(3)) decoder_1 (
    .out0(decoder_1_out0), .out1(decoder_1_out1), .out2(decoder_1_out2), .out3(decoder_1_out3),
    .out4(decoder_1_out4), .sel(ROM[6:4]), .en(Count));  // open: out5, out6, out7
  or or_1 (or_1_out, decoder_1_out1, decoder_1_out2);
  Counter counter_1 (
    .clr(decoder_1_out0), .load(SetCount), .up(or_2_out), .count(or_1_out), .clk(Clock), .D(DATA),
    .carry(CNTOverflow), .Q(counter_1_q));
  or or_2 (or_2_out, decoder_1_out1, ~decoder_1_out2);  // OR_Gate
  assign CNTOUT = s_r_ff_1_q ? counter_1_q : 8'bz;  // Controlled_Buffer controlled_buffer_1
  S_R_Flip_Flop s_r_ff_1 (
    .S(decoder_1_out3), .R(decoder_1_out4), .clk(Clock), .Q(s_r_ff_1_q));  // open: reset, Qn, preset
endmodule
